# Fritzing sketch peristaltic-pump (saved by Fritzing 0.9.2b)
circuit board: 8.46667cm x 5.64444cm

parts:
  5V_DC-DC = Mini-360 DC-DC Buck converter [package=THT]
  Часть1 = LCD1602-I2C
  A4988_Driver = A4988 Stepper Motor Driver Carrier
  Rotary_encoder_with_push_button = Rotary Encoder [package=THT]
  Arduino1 = Arduino Mini (Rev5)
  Power_Supply_12V/1A = Power plug
  R2 = Resistor [tolerance=±5% resistance=10k package=THT]
  R1 = Resistor [tolerance=±5% resistance=10k package=THT]
  R3 = Resistor [tolerance=±5% resistance=10k package=THT]
  M1 = Stepper Motor - Bipolar

nets:
  N1: 5V_DC-DC.IN-, A4988_Driver.GROUND#141, Power_Supply_12V/1A.GND
  N2: 5V_DC-DC.IN+, A4988_Driver.VMOT, Power_Supply_12V/1A.VCC
  N3: 5V_DC-DC.OUT+, Arduino1.5V
  N4: 5V_DC-DC.OUT-, Arduino1.GND
  N5: Часть1.GND, Rotary_encoder_with_push_button.EncoderPinC
  N6: Часть1.VCC, R2.Pin_0, R1.Pin_0, R3.Pin_0
  N7: Часть1.SDA, Arduino1.A4
  N8: Часть1.SCL, Arduino1.A5
  N9: A4988_Driver.Enable, Arduino1.A2
  N10: A4988_Driver.MS1, Arduino1.A1
  N11: A4988_Driver.MS2, Arduino1.A0
  N12: A4988_Driver.MS3, Arduino1.D13
  N13: A4988_Driver.RESET, Arduino1.D12
  N14: A4988_Driver.SLEEP, Arduino1.D11_PWM
  N15: A4988_Driver.STEP, Arduino1.D10_PWM
  N16: A4988_Driver.DIR, Arduino1.D9_PWM
  N17: A4988_Driver.OUT_2B, M1.C
  N18: A4988_Driver.OUT_2A, M1.A
  N19: A4988_Driver.OUT_1A, M1.B
  N20: A4988_Driver.OUT_1B, M1.D
  N21: Rotary_encoder_with_push_button.EncoderPinA, Arduino1.D3_PWM, R2.Pin_1
  N22: Rotary_encoder_with_push_button.EncoderPinB, Arduino1.D4, R1.Pin_1
  N23: Rotary_encoder_with_push_button.SwitchrPinD, Arduino1.D2, R3.Pin_1

notes:
  123

custom parts:
  Mini-360 DC-DC Buck converter: Mini-360 DC-DC Buck converter. Tiny buck step down voltage converter, input voltage 4.75 to 23V output 1 to 17V adjustable. Available from ebay and the like.
  LCD1602-I2C: A standard character display, usually with 2x16 characters. Comes in many colors with LCM1602 IIC attached.
  Rotary Encoder: Rotary Encoder from ALPSec11e with switch. This version has an alternate (which has been used in boards) pcb footprint from @opera_night in the forums. It is probably the best one to start from to see if you part matches.
